// Logisim project GabrielKimPerez_DigitalClock.circ.circ as structural Verilog
module main (
  output AM,
  output PM
);

  wire and_1_out, clock_1_out, d, day_counter_1_carry, h, j_k_ff_1_q, j_k_ff_2_qn, m, mo,
       n5_9_counter_1_out_5, n5_9_counter_2_out_5, n12_counter_1_carry, n12_counter_2_carry, not_1_out,
       not_2_out, not_3_out, OFF, on, or_1_out, or_2_out, or_3_out, or_4_out, or_5_out, s,
       year_1_leap_counter, yy0;
  wire [3:0] d0, d1, h0, h1, M0, m0_t, M1, m1_t, s0, s1, y0, y1, y2, y3;

  Frame frame_1 ();
  Hex_Digit_Display hex_digit_display_1 (.value(y3));  // open: dp
  Clock clock_1 (.out(clock_1_out));
  Hex_Digit_Display hex_digit_display_2 (.value(y2));  // open: dp
  Hex_Digit_Display hex_digit_display_3 (.value(y1));  // open: dp
  year year_1 (
    .out_3(y3), .out_4(y2), .out_5(y1), .out_6(y0), .in_1(yy0), .CLOCK(n12_counter_1_carry),
    .Leap_Counter(year_1_leap_counter));
  not not_1 (not_1_out, OFF);
  Button Y (.out(yy0));
  Hex_Digit_Display hex_digit_display_4 (.value(y0));  // open: dp
  J_K_Flip_Flop j_k_ff_1 (.J(on), .clk(on), .K(not_2_out), .Q(j_k_ff_1_q));  // open: Qn, preset, en, reset
  not not_2 (not_2_out, on);
  J_K_Flip_Flop j_k_ff_2 (.J(OFF), .clk(OFF), .K(not_1_out), .Qn(j_k_ff_2_qn));  // open: Q, preset, en, reset
  Button u_MO (.out(mo));
  Hex_Digit_Display hex_digit_display_5 (.value(M1));  // open: dp
  Hex_Digit_Display hex_digit_display_6 (.value(M0));  // open: dp
  _12_counter u_12_counter_1 (.Carry(n12_counter_1_carry), .display(M1), .display_2(M0), .CLK(or_1_out));
  or or_1 (or_1_out, mo, day_counter_1_carry);
  Hex_Digit_Display hex_digit_display_7 (.value(d1));  // open: dp
  and and_1 (and_1_out, j_k_ff_1_q, j_k_ff_2_qn, clock_1_out);
  Button u_D (.out(d));
  Hex_Digit_Display hex_digit_display_8 (.value(d0));  // open: dp
  or or_2 (or_2_out, d, AM);
  Day_counter day_counter_1 (
    .clock(or_2_out), ._2(d1), ._1(d0), .carry(day_counter_1_carry), .m1_checker(M1), .m0_checker(M0),
    .leap_checker(year_1_leap_counter));
  Button u_H (.out(h));
  Hex_Digit_Display hex_digit_display_9 (.value(h0));  // open: dp
  Hex_Digit_Display hex_digit_display_10 (.value(h1));  // open: dp
  not not_3 (not_3_out, n12_counter_2_carry);
  Hex_Digit_Display hex_digit_display_11 (.value(m0_t));  // open: dp
  Hex_Digit_Display hex_digit_display_12 (.value(m1_t));  // open: dp
  _12_counter u_12_counter_2 (.Carry(n12_counter_2_carry), .display(h1), .display_2(h0), .CLK(or_3_out));
  or or_3 (or_3_out, n5_9_counter_1_out_5, h);
  J_K_Flip_Flop j_k_ff_3 (
    .J(n12_counter_2_carry), .clk(n12_counter_2_carry), .K(not_3_out), .Q(AM), .Qn(PM));  // open: preset, en, reset
  Button u_M (.out(m));
  Hex_Digit_Display hex_digit_display_13 (.value(s1));  // open: dp
  _5_9_counter u_5_9_counter_1 (
    .out_5(n5_9_counter_1_out_5), .display(m1_t), .display_2(m0_t), .in_2(or_5_out), .ON_SWITCH(j_k_ff_1_q));
  Button u_S (.out(s));
  Hex_Digit_Display hex_digit_display_14 (.value(s0));  // open: dp
  or or_4 (or_4_out, and_1_out, s);
  or or_5 (or_5_out, n5_9_counter_2_out_5, m);
  _5_9_counter u_5_9_counter_2 (
    .out_5(n5_9_counter_2_out_5), .display(s1), .display_2(s0), .in_2(or_4_out), .ON_SWITCH(j_k_ff_1_q));
  Button u_ON (.out(on));
  Button u_OFF (.out(OFF));

  // Notes on the sheet:
  //   RUN AT 2 HERTZ
endmodule

module _5_9_counter (
  input  ON_SWITCH,
  input  in_2,
  output [3:0] display,
  output [3:0] display_2,
  output out_5
);

  wire counter9_1_p3, n0_5_counter_1_carry;

  and and_1 (out_5, n0_5_counter_1_carry, ON_SWITCH);
  _0_5_counter u_0_5_counter_1 (.Clock(counter9_1_p3), .display(display), .carry(n0_5_counter_1_carry));
  // counter9 counter9_1: pin names not known; wires that end beside it: display_2, in_2, counter9_1_p3
endmodule

module _12_counter (
  input  CLK,
  output [3:0] display,
  output [3:0] display_2,
  output Carry
);

  wire not_1_out, not_2_out, not_3_out;

  and and_1 (Carry, display[0], not_1_out, not_2_out, display_2[1], not_3_out);
  not not_1 (not_1_out, display_2[3]);
  not not_2 (not_2_out, display_2[2]);
  not not_3 (not_3_out, display_2[0]);
  _0_9_and_0_2 u_0_9_and_0_2_1 (.Clock(CLK), .display(display_2), .Carry(display[0]));

  assign display[3:1] = 3'b000;
endmodule

module _0_9_and_0_2 (
  input  Clock,
  output [3:0] display,
  output Carry
);

  wire and_1_out, and_2_out, and_3_out, and_4_out, and_5_out, and_6_out, and_7_out, and_8_out, and_9_out,
       not_1_out, not_2_out, not_3_out, not_4_out, not_5_out, not_6_out, not_7_out, not_8_out, not_9_out,
       not_10_out, not_11_out, not_12_out, not_13_out, not_14_out, not_15_out, not_16_out, not_17_out,
       not_18_out, not_19_out, not_20_out, not_21_out, not_22_out, not_23_out, not_24_out, not_25_out,
       not_26_out, or_1_out, or_2_out, or_3_out, or_4_out, reset, x, y;

  not not_1 (not_1_out, display[3]);
  not not_2 (not_2_out, display[2]);
  not not_3 (not_3_out, display[1]);
  not not_4 (not_4_out, display[0]);
  not not_5 (not_5_out, display[3]);
  not not_6 (not_6_out, display[2]);
  not not_7 (not_7_out, display[3]);
  not not_8 (not_8_out, display[1]);
  not not_9 (not_9_out, display[3]);
  not not_10 (not_10_out, display[0]);
  not not_11 (not_11_out, display[3]);
  not not_12 (not_12_out, display[1]);
  not not_13 (not_13_out, display[3]);
  not not_14 (not_14_out, display[0]);
  not not_15 (not_15_out, display[3]);
  not not_16 (not_16_out, display[0]);
  not not_17 (not_17_out, display[2]);
  not not_18 (not_18_out, display[1]);
  not not_19 (not_19_out, display[0]);
  and and_1 (and_1_out, not_1_out, display[2], display[1], display[0]);
  and and_2 (and_2_out, display[3], not_2_out, not_3_out, not_4_out);
  and and_3 (and_3_out, not_5_out, not_6_out, display[1], display[0]);
  and and_4 (and_4_out, not_7_out, display[2], not_8_out);
  and and_5 (and_5_out, not_9_out, display[2], not_10_out);
  and and_6 (and_6_out, not_11_out, not_12_out, display[0]);
  or or_1 (or_1_out, and_6_out, and_7_out);
  and and_7 (and_7_out, not_13_out, display[1], not_14_out);
  and and_8 (and_8_out, not_15_out, not_16_out);
  or or_2 (or_2_out, and_8_out, and_9_out);
  and and_9 (and_9_out, not_17_out, not_18_out, not_19_out);
  or or_3 (or_3_out, and_1_out, and_2_out);
  or or_4 (or_4_out, and_3_out, and_4_out, and_5_out);
  D_Flip_Flop d_ff_1 (.clk(Clock), .D(or_3_out), .Q(display[3]), .reset(reset));  // open: Qn, preset, en
  D_Flip_Flop d_ff_2 (.clk(Clock), .D(or_4_out), .Q(display[2]), .reset(reset));  // open: Qn, preset, en
  D_Flip_Flop d_ff_3 (.clk(Clock), .D(or_1_out), .Q(display[1]), .reset(reset));  // open: Qn, preset, en
  D_Flip_Flop d_ff_4 (.clk(Clock), .D(or_2_out), .Q(display[0]), .preset(reset));  // open: Qn, en, reset
  not not_20 (not_20_out, display[3]);
  not not_21 (not_21_out, display[2]);
  not not_22 (not_22_out, display[1]);
  not not_23 (not_23_out, display[0]);
  not not_24 (not_24_out, display[3]);
  not not_25 (not_25_out, display[2]);
  and and_10 (x, not_20_out, not_21_out, not_22_out, not_23_out);
  Hex_Digit_Display hex_digit_display_1 (.value(display));  // open: dp
  J_K_Flip_Flop j_k_ff_1 (.J(x), .clk(x), .K(not_26_out), .Q(Carry), .reset(reset));  // open: Qn, preset, en
  not not_26 (not_26_out, x);
  not not_27 (y, Carry);
  and and_11 (reset, Carry, not_24_out, not_25_out, display[1], display[0]);

  // Other names for the same wires on the sheet: Q0 = display[0]; b1 = display[1]; Q1 = display[1]; b2 = display[2];
  //   Q2 = display[2]; b3 = display[3]; Q3 = display[3]

  // Notes on the sheet:
  //   x
  //   y
endmodule

module Day_counter (
  input  [3:0] m1_checker,
  input  [3:0] m0_checker,
  input  leap_checker,
  input  clock,
  output [3:0] _2,
  output [3:0] _1,
  output carry
);

  wire _28_out, _29_out, _30_out, _31_out, and_1_out, and_2_out, and_3_out, and_4_out, and_5_out, and_6_out,
       and_7_out, and_8_out, and_9_out, and_10_out, and_11_out, and_12_out, and_13_out, and_14_out, Carry_t,
       not_1_out, not_2_out, not_3_out, not_4_out, not_5_out, not_6_out, not_7_out, not_8_out, not_9_out,
       not_10_out, not_11_out, not_12_out, not_13_out, not_14_out, not_15_out, not_16_out, not_17_out,
       not_18_out, not_19_out, not_20_out, not_21_out, not_22_out, not_23_out, not_24_out, not_25_out,
       not_26_out, not_27_out, not_28_out, not_29_out, not_30_out, not_31_out, not_32_out, not_33_out,
       not_34_out, not_35_out, not_36_out, not_37_out, not_38_out, not_39_out, not_40_out, not_41_out,
       not_42_out, not_43_out, not_44_out, or_1_out, or_2_out, or_3_out, or_4_out, R_at_0_out, R_at_9_out,
       reset;

  not not_1 (not_1_out, _2[3]);
  not not_2 (not_2_out, _2[2]);
  not not_3 (not_3_out, _2[1]);
  not not_4 (not_4_out, _2[0]);
  not not_5 (not_5_out, _2[3]);
  not not_6 (not_6_out, _2[2]);
  not not_7 (not_7_out, _2[3]);
  not not_8 (not_8_out, _2[1]);
  not not_9 (not_9_out, _2[3]);
  not not_10 (not_10_out, _2[0]);
  not not_11 (not_11_out, _2[3]);
  not not_12 (not_12_out, _2[1]);
  not not_13 (not_13_out, _2[3]);
  not not_14 (not_14_out, _2[0]);
  not not_15 (not_15_out, _2[3]);
  not not_16 (not_16_out, _2[0]);
  not not_17 (not_17_out, _2[2]);
  not not_18 (not_18_out, _2[1]);
  not not_19 (not_19_out, _2[0]);
  and and_1 (and_1_out, not_1_out, _2[2], _2[1], _2[0]);
  and and_2 (and_2_out, _2[3], not_2_out, not_3_out, not_4_out);
  and and_3 (and_3_out, not_5_out, not_6_out, _2[1], _2[0]);
  and and_4 (and_4_out, not_7_out, _2[2], not_8_out);
  and and_5 (and_5_out, not_9_out, _2[2], not_10_out);
  and and_6 (and_6_out, not_11_out, not_12_out, _2[0]);
  and and_7 (and_7_out, not_13_out, _2[1], not_14_out);
  and and_8 (and_8_out, not_15_out, not_16_out);
  and and_9 (and_9_out, not_17_out, not_18_out, not_19_out);
  or or_1 (or_1_out, and_1_out, and_2_out);
  or or_2 (or_2_out, and_3_out, and_4_out, and_5_out);
  or or_3 (or_3_out, and_6_out, and_7_out);
  or or_4 (or_4_out, and_8_out, and_9_out);
  D_Flip_Flop d_ff_1 (.clk(Carry_t), .D(or_1_out), .Q(_2[3]), .reset(reset));  // open: Qn, preset, en
  D_Flip_Flop d_ff_2 (.clk(Carry_t), .D(or_2_out), .Q(_2[2]), .reset(reset));  // open: Qn, preset, en
  D_Flip_Flop d_ff_3 (.clk(Carry_t), .D(or_3_out), .Q(_2[1]), .reset(reset));  // open: Qn, preset, en
  D_Flip_Flop d_ff_4 (.clk(Carry_t), .D(or_4_out), .Q(_2[0]), .reset(reset));  // open: Qn, preset, en
  resettable_0_9 resettable_0_9_1 (.RESET(reset), .Clock(clock), .display(_1), .Carry(Carry_t));
  not not_20 (not_20_out, _1[1]);
  not not_21 (not_21_out, _1[2]);
  and R_at_9 (R_at_9_out, _1[0], not_20_out, not_21_out, _1[3]);
  not not_22 (not_22_out, _1[0]);
  not not_23 (not_23_out, _1[1]);
  not not_24 (not_24_out, _1[2]);
  not not_25 (not_25_out, _1[3]);
  not not_26 (not_26_out, _2[3]);
  not not_27 (not_27_out, _2[2]);
  not not_28 (not_28_out, _2[1]);
  not not_29 (not_29_out, _2[0]);
  and and_10 (and_10_out, _2[1], not_30_out);
  not not_30 (not_30_out, _2[0]);
  and and_11 (and_11_out, _2[1], _2[0]);
  and R_at_0 (R_at_0_out, not_22_out, not_23_out, not_24_out, not_25_out);
  and and_12 (and_12_out, not_32_out, m0_checker[1], and_13_out, not_33_out, not_31_out);
  not not_31 (not_31_out, m0_checker[3]);
  not not_32 (not_32_out, m0_checker[0]);
  not not_33 (not_33_out, m0_checker[2]);
  not not_34 (not_34_out, _1[1]);
  not not_35 (not_35_out, _1[2]);
  not not_36 (not_36_out, _1[3]);
  not not_37 (not_37_out, _1[1]);
  and _30 (_30_out, and_11_out, not_37_out, _1[0], not_38_out);
  not not_38 (not_38_out, m0_checker[0]);
  and _31 (_31_out, and_11_out, _1[1], not_39_out, m0_checker[0]);
  not not_39 (not_39_out, _1[0]);
  not not_40 (not_40_out, leap_checker);
  and _28 (_28_out, not_40_out, and_10_out, and_12_out, R_at_9_out);
  and _29 (_29_out, and_12_out, and_11_out, R_at_0_out, leap_checker);
  and and_13 (and_13_out, not_41_out, not_42_out, not_43_out, not_44_out);
  and and_14 (and_14_out, _1[0], not_34_out, not_35_out, not_36_out);
  not not_41 (not_41_out, m1_checker[0]);
  not not_42 (not_42_out, m1_checker[1]);
  not not_43 (not_43_out, m1_checker[2]);
  not not_44 (not_44_out, m1_checker[3]);
  and and_15 (carry, and_14_out, not_26_out, not_27_out, not_28_out, not_29_out);
  or or_5 (reset, _30_out, _31_out, _28_out, _29_out);

  // Other names for the same wires on the sheet: B0 = _1[0]; B1 = _1[1]; B2 = _1[2]; B3 = _1[3]; Q0 = _2[0];
  //   Q1 = _2[1]; Q2 = _2[2]; Q3 = _2[3]

  // Notes on the sheet:
  //   day from 0-9
  //   0-3, feb included
  //   when month is 2 and leap year carry is true, we go up to 29, otherwise 28
  //   when month is odd, we add and extra day and reset it
  //   second digit
  //   first digit
endmodule

module resettable_0_9 (
  input  Clock,
  input  RESET,
  output [3:0] display,
  output Carry
);

  wire and_1_out, and_2_out, and_3_out, and_4_out, and_5_out, and_6_out, and_7_out, and_8_out, and_9_out,
       not_1_out, not_2_out, not_3_out, not_4_out, not_5_out, not_6_out, not_7_out, not_8_out, not_9_out,
       not_10_out, not_11_out, not_12_out, not_13_out, not_14_out, not_15_out, not_16_out, not_17_out,
       not_18_out, not_19_out, not_20_out, not_21_out, not_22_out, not_23_out, or_1_out, or_2_out, or_3_out,
       or_4_out;

  not not_1 (not_1_out, display[3]);
  not not_2 (not_2_out, display[2]);
  not not_3 (not_3_out, display[1]);
  not not_4 (not_4_out, display[0]);
  not not_5 (not_5_out, display[3]);
  not not_6 (not_6_out, display[2]);
  not not_7 (not_7_out, display[3]);
  not not_8 (not_8_out, display[1]);
  not not_9 (not_9_out, display[3]);
  not not_10 (not_10_out, display[0]);
  not not_11 (not_11_out, display[3]);
  not not_12 (not_12_out, display[1]);
  and and_1 (and_1_out, not_11_out, not_12_out, display[0]);
  not not_13 (not_13_out, display[3]);
  and and_2 (and_2_out, not_13_out, display[1], not_14_out);
  not not_14 (not_14_out, display[0]);
  not not_15 (not_15_out, display[3]);
  and and_3 (and_3_out, not_15_out, not_16_out);
  not not_16 (not_16_out, display[0]);
  not not_17 (not_17_out, display[2]);
  and and_4 (and_4_out, not_17_out, not_18_out, not_19_out);
  not not_18 (not_18_out, display[1]);
  not not_19 (not_19_out, display[0]);
  and and_5 (and_5_out, not_1_out, display[2], display[1], display[0]);
  or or_1 (or_1_out, and_5_out, and_6_out);
  and and_6 (and_6_out, display[3], not_2_out, not_3_out, not_4_out);
  and and_7 (and_7_out, not_5_out, not_6_out, display[1], display[0]);
  or or_2 (or_2_out, and_7_out, and_8_out, and_9_out);
  and and_8 (and_8_out, not_7_out, display[2], not_8_out);
  and and_9 (and_9_out, not_9_out, display[2], not_10_out);
  or or_3 (or_3_out, and_1_out, and_2_out);
  or or_4 (or_4_out, and_3_out, and_4_out);
  D_Flip_Flop d_ff_1 (.clk(Clock), .D(or_1_out), .Q(display[3]), .reset(RESET));  // open: Qn, preset, en
  D_Flip_Flop d_ff_2 (.clk(Clock), .D(or_2_out), .Q(display[2]), .reset(RESET));  // open: Qn, preset, en
  D_Flip_Flop d_ff_3 (.clk(Clock), .D(or_3_out), .Q(display[1]), .reset(RESET));  // open: Qn, preset, en
  D_Flip_Flop d_ff_4 (.clk(Clock), .D(or_4_out), .Q(display[0]), .preset(RESET));  // open: Qn, en, reset
  not not_20 (not_20_out, display[3]);
  not not_21 (not_21_out, display[2]);
  not not_22 (not_22_out, display[1]);
  not not_23 (not_23_out, display[0]);
  and and_10 (Carry, not_20_out, not_21_out, not_22_out, not_23_out);

  // Other names for the same wires on the sheet: Carry_t = RESET; Q0 = display[0]; Q1 = display[1]; Q2 = display[2];
  //   Q3 = display[3]
endmodule

module Leap_counter (
  input  Clock,
  output [3:0] display,
  output Carry
);

  wire and_1_out, and_2_out, and_3_out, and_4_out, and_5_out, and_6_out, and_7_out, and_8_out, and_9_out,
       not_1_out, not_2_out, not_3_out, not_4_out, not_5_out, not_6_out, not_7_out, not_8_out, not_9_out,
       not_10_out, not_11_out, not_12_out, not_13_out, not_14_out, not_15_out, not_16_out, not_17_out,
       not_18_out, not_19_out, not_20_out, not_21_out, not_22_out, not_23_out, not_24_out, not_25_out,
       not_26_out, or_1_out, or_2_out, or_3_out, or_4_out, reset;

  not not_1 (not_1_out, display[3]);
  not not_2 (not_2_out, display[2]);
  not not_3 (not_3_out, display[1]);
  not not_4 (not_4_out, display[0]);
  not not_5 (not_5_out, display[3]);
  not not_6 (not_6_out, display[2]);
  not not_7 (not_7_out, display[3]);
  not not_8 (not_8_out, display[1]);
  not not_9 (not_9_out, display[3]);
  not not_10 (not_10_out, display[0]);
  not not_11 (not_11_out, display[3]);
  not not_12 (not_12_out, display[0]);
  not not_13 (not_13_out, display[2]);
  not not_14 (not_14_out, display[1]);
  not not_15 (not_15_out, display[0]);
  and and_1 (and_1_out, not_1_out, display[2], display[1], display[0]);
  and and_2 (and_2_out, display[3], not_2_out, not_3_out, not_4_out);
  and and_3 (and_3_out, not_5_out, not_6_out, display[1], display[0]);
  not not_16 (not_16_out, display[3]);
  and and_4 (and_4_out, not_16_out, display[2], not_17_out);
  not not_17 (not_17_out, display[1]);
  not not_18 (not_18_out, display[3]);
  and and_5 (and_5_out, not_18_out, display[2], not_19_out);
  not not_19 (not_19_out, display[0]);
  and and_6 (and_6_out, not_7_out, not_8_out, display[0]);
  and and_7 (and_7_out, not_9_out, display[1], not_10_out);
  and and_8 (and_8_out, not_11_out, not_12_out);
  and and_9 (and_9_out, not_13_out, not_14_out, not_15_out);
  or or_1 (or_1_out, and_1_out, and_2_out);
  or or_2 (or_2_out, and_3_out, and_4_out, and_5_out);
  or or_3 (or_3_out, and_6_out, and_7_out);
  or or_4 (or_4_out, and_8_out, and_9_out);
  D_Flip_Flop d_ff_1 (.clk(Clock), .D(or_1_out), .Q(display[3]), .reset(reset));  // open: Qn, preset, en
  D_Flip_Flop d_ff_2 (.clk(Clock), .D(or_2_out), .Q(display[2]), .reset(reset));  // open: Qn, preset, en
  D_Flip_Flop d_ff_3 (.clk(Clock), .D(or_3_out), .Q(display[1]), .reset(reset));  // open: Qn, preset, en
  D_Flip_Flop d_ff_4 (.clk(Clock), .D(or_4_out), .Q(display[0]), .reset(reset));  // open: Qn, preset, en
  not not_20 (not_20_out, display[0]);
  not not_21 (not_21_out, display[1]);
  not not_22 (not_22_out, display[2]);
  not not_23 (not_23_out, display[3]);
  not not_24 (not_24_out, display[3]);
  not not_25 (not_25_out, display[1]);
  not not_26 (not_26_out, display[0]);
  and and_10 (reset, not_24_out, display[2], not_25_out, not_26_out);
  and and_11 (Carry, not_20_out, not_21_out, not_22_out, not_23_out);

  // Other names for the same wires on the sheet: Q0 = display[0]; Q1 = display[1]; Q2 = display[2]; Q3 = display[3]
endmodule

module year (
  input  in_1,
  input  CLOCK,
  output [3:0] out_3,
  output [3:0] out_4,
  output [3:0] out_5,
  output [3:0] out_6,
  output Leap_Counter
);

  wire counter9_1_p2, counter9_2_p2, counter9_3_p3, or_2_out;

  // counter9 counter9_1: pin names not known; wires that end beside it: out_3, counter9_1_p2
  // counter9 counter9_2: pin names not known; wires that end beside it: out_4, counter9_2_p2
  // counter9 counter9_3: pin names not known; wires that end beside it: counter9_1_p2, out_5, counter9_3_p3
  // counter9 counter9_4: pin names not known; wires that end beside it: counter9_2_p2, out_6, counter9_3_p3
  // OR_Gate or_1 has open pins: in0=in_1, in1=CLOCK, out=open
  or or_2 (or_2_out, CLOCK, in_1);
  Leap_counter leap_counter_1 (.Clock(or_2_out), .Carry(Leap_Counter));  // open: display
endmodule

module _0_5_counter (
  input  Clock,
  output [3:0] display,
  output carry
);

  wire and_1_out, and_2_out, and_3_out, and_4_out, and_5_out, and_6_out, and_7_out, and_8_out, and_9_out,
       and_11_out, not_1_out, not_2_out, not_3_out, not_4_out, not_5_out, not_6_out, not_7_out, not_8_out,
       not_9_out, not_10_out, not_11_out, not_12_out, not_13_out, not_14_out, not_15_out, not_16_out,
       not_17_out, not_18_out, not_19_out, not_20_out, not_21_out, not_22_out, not_23_out, or_1_out,
       or_2_out, or_3_out, or_4_out, reset;

  not not_1 (not_1_out, display[3]);
  not not_2 (not_2_out, display[2]);
  not not_3 (not_3_out, display[1]);
  not not_4 (not_4_out, display[0]);
  not not_5 (not_5_out, display[3]);
  not not_6 (not_6_out, display[2]);
  not not_7 (not_7_out, display[3]);
  not not_8 (not_8_out, display[1]);
  not not_9 (not_9_out, display[3]);
  not not_10 (not_10_out, display[0]);
  not not_11 (not_11_out, display[3]);
  not not_12 (not_12_out, display[0]);
  not not_13 (not_13_out, display[2]);
  not not_14 (not_14_out, display[1]);
  not not_15 (not_15_out, display[0]);
  and and_1 (and_1_out, not_1_out, display[2], display[1], display[0]);
  and and_2 (and_2_out, display[3], not_2_out, not_3_out, not_4_out);
  and and_3 (and_3_out, not_5_out, not_6_out, display[1], display[0]);
  not not_16 (not_16_out, display[3]);
  and and_4 (and_4_out, not_16_out, display[2], not_17_out);
  not not_17 (not_17_out, display[1]);
  not not_18 (not_18_out, display[3]);
  and and_5 (and_5_out, not_18_out, display[2], not_19_out);
  not not_19 (not_19_out, display[0]);
  and and_6 (and_6_out, not_7_out, not_8_out, display[0]);
  and and_7 (and_7_out, not_9_out, display[1], not_10_out);
  and and_8 (and_8_out, not_11_out, not_12_out);
  and and_9 (and_9_out, not_13_out, not_14_out, not_15_out);
  or or_1 (or_1_out, and_1_out, and_2_out);
  or or_2 (or_2_out, and_3_out, and_4_out, and_5_out);
  or or_3 (or_3_out, and_6_out, and_7_out);
  or or_4 (or_4_out, and_8_out, and_9_out);
  D_Flip_Flop d_ff_1 (.clk(Clock), .D(or_1_out), .Q(display[3]), .reset(reset));  // open: Qn, preset, en
  D_Flip_Flop d_ff_2 (.clk(Clock), .D(or_2_out), .Q(display[2]), .reset(reset));  // open: Qn, preset, en
  D_Flip_Flop d_ff_3 (.clk(Clock), .D(or_3_out), .Q(display[1]), .reset(reset));  // open: Qn, preset, en
  D_Flip_Flop d_ff_4 (.clk(Clock), .D(or_4_out), .Q(display[0]), .reset(reset));  // open: Qn, preset, en
  and and_10 (reset, ~display[3], display[2], display[1], ~display[0]);  // AND_Gate
  not not_20 (not_20_out, display[3]);
  not not_21 (not_21_out, display[2]);
  and and_11 (and_11_out, not_20_out, not_21_out, not_22_out, not_23_out);
  not not_22 (not_22_out, display[1]);
  not not_23 (not_23_out, display[0]);
  buf and_12 (carry, and_11_out);  // AND_Gate

  // Other names for the same wires on the sheet: Q0 = display[0]; Q1 = display[1]; Q2 = display[2]; Q3 = display[3]
endmodule
