// Logisim project clock.circ as structural Verilog: 2 circuits, main circuit main
module main (
  input  in_1,
  input  in_2,
  input  in_3,
  input  in_4,
  input  in_5,
  input  in_6,
  input  in_7,
  input  in_8
);

  wire [2:1] undriven;
  wire [3:3] multiplexer_1_out;

  Multiplexer #(.select(3)) multiplexer_1 (
    .in0(in_1), .in1(in_2), .in2(in_3), .in3(in_4), .in4(in_5), .in5(in_6), .in6(in_7), .in7(in_8),
    .out(multiplexer_1_out[3]), .sel({undriven, 1'b1}));  // open: en
  Hex_Digit_Display hex_digit_display_1 (.value({4{multiplexer_1_out[3]}}));  // open: dp
  // Pins of 1 and 3 bits meet at {undriven, 1'b1}
endmodule

module second_bit (
  input  in_1,
  output out_2
);

  wire not_1_out;

  not not_1 (not_1_out, in_1);
  J_K_Flip_Flop j_k_ff_1 (.J(in_1), .clk(in_1), .K(not_1_out), .Q(out_2));  // open: Qn, preset, en, reset
endmodule
